# Fritzing sketch NautiControlSTWireless (saved by Fritzing 0.9.10b)
circuit board: 10cm x 7cm
breadboards: 1

parts:
  IC1_A = 74LS04 [chip_label=IC package="DIP (Dual Inline) [THT]"]  # not connected
  IC1_B = 74LS04 [chip_label=IC package="DIP (Dual Inline) [THT]"]  # not connected
  IC1_C = 74LS04 [chip_label=IC package="DIP (Dual Inline) [THT]"]  # not connected
  IC1_D = 74LS04 [chip_label=IC package="DIP (Dual Inline) [THT]"]  # not connected
  IC1_E = 74LS04 [chip_label=IC package="DIP (Dual Inline) [THT]"]  # not connected
  IC1_F = 74LS04 [chip_label=IC package="DIP (Dual Inline) [THT]"]  # not connected
  IC1_PWR = 74LS04 [chip_label=IC package="DIP (Dual Inline) [THT]"]  # not connected
  IC2_A = 74LS04 [chip_label=IC package="DIP (Dual Inline) [THT]"]  # not connected
  IC2_B = 74LS04 [chip_label=IC package="DIP (Dual Inline) [THT]"]  # not connected
  IC2_C = 74LS04 [chip_label=IC package="DIP (Dual Inline) [THT]"]  # not connected
  IC2_D = 74LS04 [chip_label=IC package="DIP (Dual Inline) [THT]"]  # not connected
  IC2_E = 74LS04 [chip_label=IC package="DIP (Dual Inline) [THT]"]  # not connected
  IC2_F = 74LS04 [chip_label=IC package="DIP (Dual Inline) [THT]"]  # not connected
  IC2_PWR = 74LS04 [chip_label=IC package="DIP (Dual Inline) [THT]"]  # not connected
  IC2_A_2 = 74LS04 [chip_label=IC package="DIP (Dual Inline) [THT]"]  # not connected
  IC2_B_2 = 74LS04 [chip_label=IC package="DIP (Dual Inline) [THT]"]  # not connected
  IC2_C_2 = 74LS04 [chip_label=IC package="DIP (Dual Inline) [THT]"]  # not connected
  IC2_D_2 = 74LS04 [chip_label=IC package="DIP (Dual Inline) [THT]"]  # not connected
  IC2_E_2 = 74LS04 [chip_label=IC package="DIP (Dual Inline) [THT]"]  # not connected
  IC2_F_2 = 74LS04 [chip_label=IC package="DIP (Dual Inline) [THT]"]  # not connected
  IC2_PWR_2 = 74LS04 [chip_label=IC package="DIP (Dual Inline) [THT]"]  # not connected
  IC1_A_2 = 74LS04 [chip_label=IC package="DIP (Dual Inline) [THT]"]  # not connected
  IC1_B_2 = 74LS04 [chip_label=IC package="DIP (Dual Inline) [THT]"]  # not connected
  IC1_C_2 = 74LS04 [chip_label=IC package="DIP (Dual Inline) [THT]"]  # not connected
  IC1_D_2 = 74LS04 [chip_label=IC package="DIP (Dual Inline) [THT]"]  # not connected
  IC1_E_2 = 74LS04 [chip_label=IC package="DIP (Dual Inline) [THT]"]  # not connected
  IC1_F_2 = 74LS04 [chip_label=IC package="DIP (Dual Inline) [THT]"]  # not connected
  IC1_PWR_2 = 74LS04 [chip_label=IC package="DIP (Dual Inline) [THT]"]  # not connected
  IC2_A_3 = 74LS04 [chip_label=IC package="DIP (Dual Inline) [THT]"]  # not connected
  IC2_B_3 = 74LS04 [chip_label=IC package="DIP (Dual Inline) [THT]"]  # not connected
  IC2_C_3 = 74LS04 [chip_label=IC package="DIP (Dual Inline) [THT]"]  # not connected
  IC2_D_3 = 74LS04 [chip_label=IC package="DIP (Dual Inline) [THT]"]  # not connected
  IC2_E_3 = 74LS04 [chip_label=IC package="DIP (Dual Inline) [THT]"]  # not connected
  IC2_F_3 = 74LS04 [chip_label=IC package="DIP (Dual Inline) [THT]"]  # not connected
  IC2_PWR_3 = 74LS04 [chip_label=IC package="DIP (Dual Inline) [THT]"]  # not connected
  IC2_A_4 = 74LS04 [chip_label=IC package="DIP (Dual Inline) [THT]"]  # not connected
  IC2_B_4 = 74LS04 [chip_label=IC package="DIP (Dual Inline) [THT]"]  # not connected
  IC2_C_4 = 74LS04 [chip_label=IC package="DIP (Dual Inline) [THT]"]  # not connected
  IC2_D_4 = 74LS04 [chip_label=IC package="DIP (Dual Inline) [THT]"]  # not connected
  IC2_E_4 = 74LS04 [chip_label=IC package="DIP (Dual Inline) [THT]"]  # not connected
  IC2_F_4 = 74LS04 [chip_label=IC package="DIP (Dual Inline) [THT]"]  # not connected
  IC2_PWR_4 = 74LS04 [chip_label=IC package="DIP (Dual Inline) [THT]"]  # not connected
  IC1_A_3 = 74LS04 [chip_label=IC package="DIP (Dual Inline) [THT]"]  # not connected
  IC1_B_3 = 74LS04 [chip_label=IC package="DIP (Dual Inline) [THT]"]  # not connected
  IC1_C_3 = 74LS04 [chip_label=IC package="DIP (Dual Inline) [THT]"]  # not connected
  IC1_D_3 = 74LS04 [chip_label=IC package="DIP (Dual Inline) [THT]"]  # not connected
  IC1_E_3 = 74LS04 [chip_label=IC package="DIP (Dual Inline) [THT]"]  # not connected
  IC1_F_3 = 74LS04 [chip_label=IC package="DIP (Dual Inline) [THT]"]  # not connected
  IC1_PWR_3 = 74LS04 [chip_label=IC package="DIP (Dual Inline) [THT]"]  # not connected
  IC2_A_5 = 74LS04 [chip_label=IC package="DIP (Dual Inline) [THT]"]  # not connected
  IC2_B_5 = 74LS04 [chip_label=IC package="DIP (Dual Inline) [THT]"]  # not connected
  IC2_C_5 = 74LS04 [chip_label=IC package="DIP (Dual Inline) [THT]"]  # not connected
  IC2_D_5 = 74LS04 [chip_label=IC package="DIP (Dual Inline) [THT]"]  # not connected
  IC2_E_5 = 74LS04 [chip_label=IC package="DIP (Dual Inline) [THT]"]  # not connected
  IC2_F_5 = 74LS04 [chip_label=IC package="DIP (Dual Inline) [THT]"]  # not connected
  IC2_PWR_5 = 74LS04 [chip_label=IC package="DIP (Dual Inline) [THT]"]  # not connected
  IC2_A_6 = 74LS04 [chip_label=IC package="DIP (Dual Inline) [THT]"]  # not connected
  IC2_B_6 = 74LS04 [chip_label=IC package="DIP (Dual Inline) [THT]"]  # not connected
  IC2_C_6 = 74LS04 [chip_label=IC package="DIP (Dual Inline) [THT]"]  # not connected
  IC2_D_6 = 74LS04 [chip_label=IC package="DIP (Dual Inline) [THT]"]  # not connected
  IC2_E_6 = 74LS04 [chip_label=IC package="DIP (Dual Inline) [THT]"]  # not connected
  IC2_F_6 = 74LS04 [chip_label=IC package="DIP (Dual Inline) [THT]"]  # not connected
  IC2_PWR_6 = 74LS04 [chip_label=IC package="DIP (Dual Inline) [THT]"]  # not connected
  IC1_A_4 = 74LS04 [chip_label=IC package="DIP (Dual Inline) [THT]"]  # not connected
  IC1_B_4 = 74LS04 [chip_label=IC package="DIP (Dual Inline) [THT]"]  # not connected
  IC1_C_4 = 74LS04 [chip_label=IC package="DIP (Dual Inline) [THT]"]  # not connected
  IC1_D_4 = 74LS04 [chip_label=IC package="DIP (Dual Inline) [THT]"]  # not connected
  IC1_E_4 = 74LS04 [chip_label=IC package="DIP (Dual Inline) [THT]"]  # not connected
  IC1_F_4 = 74LS04 [chip_label=IC package="DIP (Dual Inline) [THT]"]  # not connected
  IC1_PWR_4 = 74LS04 [chip_label=IC package="DIP (Dual Inline) [THT]"]  # not connected
  IC2_A_7 = 74LS04 [chip_label=IC package="DIP (Dual Inline) [THT]"]  # not connected
  IC2_B_7 = 74LS04 [chip_label=IC package="DIP (Dual Inline) [THT]"]  # not connected
  IC2_C_7 = 74LS04 [chip_label=IC package="DIP (Dual Inline) [THT]"]  # not connected
  IC2_D_7 = 74LS04 [chip_label=IC package="DIP (Dual Inline) [THT]"]  # not connected
  IC2_E_7 = 74LS04 [chip_label=IC package="DIP (Dual Inline) [THT]"]  # not connected
  IC2_F_7 = 74LS04 [chip_label=IC package="DIP (Dual Inline) [THT]"]  # not connected
  IC2_PWR_7 = 74LS04 [chip_label=IC package="DIP (Dual Inline) [THT]"]  # not connected
  IC2_A_8 = 74LS04 [chip_label=IC package="DIP (Dual Inline) [THT]"]  # not connected
  IC2_B_8 = 74LS04 [chip_label=IC package="DIP (Dual Inline) [THT]"]  # not connected
  IC2_C_8 = 74LS04 [chip_label=IC package="DIP (Dual Inline) [THT]"]  # not connected
  IC2_D_8 = 74LS04 [chip_label=IC package="DIP (Dual Inline) [THT]"]  # not connected
  IC2_E_8 = 74LS04 [chip_label=IC package="DIP (Dual Inline) [THT]"]  # not connected
  IC2_F_8 = 74LS04 [chip_label=IC package="DIP (Dual Inline) [THT]"]  # not connected
  IC2_PWR_8 = 74LS04 [chip_label=IC package="DIP (Dual Inline) [THT]"]  # not connected
  IC1_A_5 = 74LS04 [chip_label=IC package="DIP (Dual Inline) [THT]"]  # not connected
  IC1_B_5 = 74LS04 [chip_label=IC package="DIP (Dual Inline) [THT]"]  # not connected
  IC1_C_5 = 74LS04 [chip_label=IC package="DIP (Dual Inline) [THT]"]  # not connected
  IC1_D_5 = 74LS04 [chip_label=IC package="DIP (Dual Inline) [THT]"]  # not connected
  IC1_F_5 = 74LS04 [chip_label=IC package="DIP (Dual Inline) [THT]"]  # not connected
  IC1_PWR_5 = 74LS04 [chip_label=IC package="DIP (Dual Inline) [THT]"]  # not connected
  PC817 = IC, DIP package, 4 pins [chip_label=PC817]
  2 = female pin header, 4 pins [form="♀ (female)"]
  433mhz = female pin header, 4 pins [form="♀ (female)"]
  10kΩ = Resistor [tolerance=±5% power=0.25 resistance=10k package=THT]
  270Ω = Resistor [tolerance=±5% power=0.25 resistance=270 package=THT]
  10kΩ_2 = Resistor [tolerance=±5% power=0.25 resistance=10k package=THT]
  1kΩ = Resistor [tolerance=±5% power=0.25 resistance=1k package=THT]
  BC_547 = NPN-Transistor [package="TO92 [THT]"]
  3_9kΩ = Resistor [tolerance=±5% power=0.25 resistance=3.9k package=THT]
  270Ω_2 = Resistor [tolerance=±5% power=0.25 resistance=270 package=THT]
  7805 = Voltage Regulator [package=to220-igo]
  J1 = female pin header, 3 pins [form="♀ (female)"]
  Ant = female pin header, 1 pin [form="♀ (female)"]
  J1_2 = female pin header, 3 pins [form="♀ (female)"]
  10kΩ_3 = Resistor [tolerance=±5% power=0.25 resistance=10k package=THT]
  PWR = LED - 5mm [color="Red (633nm)" current=0.030 package="5 mm [THT]"]
  PC817_2 = IC, DIP package, 4 pins [chip_label=PC817]
  ESP32 = LuaNode32 / ESP32 [part_number=ESP32S-PIN30]

nets:
  N1: PC817.pin1, 1kΩ.Pin_1
  N2: PC817.pin2, BC_547.C
  GND: PC817.pin3, 2.pin2, 2.pin3, 433mhz.pin4, BC_547.E, 3_9kΩ.Pin_1, 7805.GND, J1.pin3, J1_2.pin3, PWR.cathode, PC817_2.pin2, PC817_2.pin3, ESP32.GND
  N3: PC817.pin4, 10kΩ.Pin_1, ESP32.D32
  N4: 2.pin1, Ant.pin1
  N5: 2.pin4, 7805.OUT, ESP32.Vin
  N6: 433mhz.pin1, 270Ω_2.Pin_0
  N7: 433mhz.pin3, ESP32.D34
  N8: 10kΩ.Pin_0, ESP32.3V3
  N9: 270Ω.Pin_0, PC817_2.pin1
  N10: 270Ω.Pin_1, ESP32.D33
  N11: 10kΩ_2.Pin_0, J1_2.pin2, 10kΩ_3.Pin_1, PC817_2.pin4
  N12: 10kΩ_2.Pin_1, BC_547.B, 3_9kΩ.Pin_0
  N13: 1kΩ.Pin_0, 7805.IN, J1_2.pin1, 10kΩ_3.Pin_0
  N14: 270Ω_2.Pin_1, PWR.anode
  N15: J1.pin1, ESP32.TX0
  N16: J1.pin2, ESP32.RX0

notes:
  Copyright 2023
  www.nauti-control.com
  -
  +
  D

custom parts:
  74LS04: Hex Inverter
  74LS04: Hex Inverter
  74LS04: Hex Inverter
  74LS04: Hex Inverter
  74LS04: Hex Inverter
  74LS04: Hex Inverter
  74LS04: Hex Inverter
  74LS04: Hex Inverter
  74LS04: Hex Inverter
  74LS04: Hex Inverter
  74LS04: Hex Inverter
  74LS04: Hex Inverter
  74LS04: Hex Inverter
  74LS04: Hex Inverter
  74LS04: Hex Inverter
  74LS04: Hex Inverter
  74LS04: Hex Inverter
  74LS04: Hex Inverter
  74LS04: Hex Inverter
  74LS04: Hex Inverter
  74LS04: Hex Inverter
  74LS04: Hex Inverter
  74LS04: Hex Inverter
  74LS04: Hex Inverter
  74LS04: Hex Inverter
  74LS04: Hex Inverter
  74LS04: Hex Inverter
  74LS04: Hex Inverter
  LuaNode32 / ESP32: New Image for LuaNode32 DOIT ESP32 DEVKIT V1. Base parts from LuaNode32 / ESP32 ESP32 based LuaNode32 by G.Noorlander DOIT Esp32 DevKit v1 (30 pins long, 11 pins width) by Werner Rothschopf (modified by vanepp Dec 2018)
